# Fritzing sketch robiohead_M3 (saved by Fritzing 0.9.4)
breadboards: 1

parts:
  Bela1 = Bela
  Part5 = Triple Axis Accelerometer Breakout - ADXL335
  R1 = Basic Flex Resistor
  LSM9DS2 = SparkFun-LSM9DS1-Breakout [part_number=SEN-13284]  # not connected
  R6 = Resistor [tolerance=±5% resistance=47k package="2010 [SMD]"]
  SparkFun2 = SoftPot Membrane Potentiometer - 50mm [part_number=SEN-08680]
  S2 = Pushbutton [package="[THT]"]
  R7 = Resistor [tolerance=±5% resistance=10k package=THT]
  LED2 = LED - 5mm [color="Red (633nm)" package="5 mm [THT]"]
  R8 = Resistor [tolerance=±5% resistance=220 package=THT]

nets:
  N1: Bela1.P9_01_GND, Part5.GND, R6.Pin_1, SparkFun2.leg1, R7.Pin_1, R8.Pin_1
  N2: Bela1.P9_03_3.3V, Part5.VCC, R1.Pin_2, SparkFun2.leg2, S2.Pin_3, S2.Pin_4
  N3: Bela1.P9_13, LED2.anode
  N4: Bela1.P9_14_D7, S2.Pin_1, S2.Pin_2, R7.Pin_0
  N5: Bela1.AIN_2, Part5.YOUT
  N6: Bela1.AIN_1, R1.pin_1, R6.Pin_0
  N7: Bela1.AIN_0, SparkFun2.wiper
  N8: LED2.cathode, R8.Pin_0

custom parts:
  Bela: A Fritzing part for Bela
  SparkFun-LSM9DS1-Breakout: The LSM9DS1 is a versatile, motion-sensing system-in-a-chip. It houses a 3-axis accelerometer, 3-axis gyroscope, and 3-axis magnetometer – nine degrees of freedom (9DOF) in a single IC! The LSM9DS1 is equipped with a digital interface, but even that is flexible: it supports both I2C and SPI, so you’ll be hard-pressed to find a microcontroller it doesn’t work with. Each sensor in the LSM9DS1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
  SoftPot Membrane Potentiometer - 50mm: These are very thin variable potentiometers. By pressing down on various parts of the strip, the resistance linearly changes from 100Ohms to 10,000Ohms allowing the user to very accurately calculate the relative position on the strip. Can be used as an accurate positional indicator for CNC head positioning, variable user input (volume level input for example), straight user input (multiple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
