# Fritzing sketch robiohead_MCT_final (saved by Fritzing 0.9.4)
breadboards: 1

parts:
  Bela1 = Bela
  Part5 = Triple Axis Accelerometer Breakout - ADXL335
  R1 = Basic Flex Resistor
  LSM9DS2 = SparkFun-LSM9DS1-Breakout [part_number=SEN-13284]  # not connected
  R6 = Resistor [tolerance=±5% resistance=47k package="2010 [SMD]"]
  SparkFun2 = SoftPot Membrane Potentiometer - 50mm [part_number=SEN-08680]
  S2 = Pushbutton [package="[THT]"]
  R7 = Resistor [tolerance=±5% resistance=10k package=THT]
  R8 = Resistor [tolerance=±5% resistance=220 package=THT]
  R9 = Rotary Potentiometer (Small) [maximum_resistance=100kΩ package=THT]
  R10 = Slide Potentiometer [maximum_resistance=100kΩ]
  LED2 = LED - 5mm [color="Red (633nm)" package="5 mm [THT]"]
  LED3 = LED - 5mm [color="Red (633nm)" package="5 mm [THT]"]
  R11 = Resistor [tolerance=±5% resistance=220 package=THT]
  R12 = Resistor [tolerance=±5% resistance=220 package=THT]

nets:
  N1: Bela1.P9_01_GND, Part5.GND, R6.Pin_1, SparkFun2.leg1, R7.Pin_1, R8.Pin_1, R9.leg2, R10.leg2
  N2: Bela1.P9_03_3.3V, Part5.VCC, R1.Pin_2, SparkFun2.leg2, S2.Pin_3, S2.Pin_4, R9.leg1
  N3: Bela1.P9_14_D7, S2.Pin_1, S2.Pin_2, R7.Pin_0
  N4: Bela1.AIN_3, R9.wiper
  N5: Bela1.AIN_2, Part5.YOUT
  N6: Bela1.AIN_1, R1.pin_1, R6.Pin_0
  N7: Bela1.AIN_0, SparkFun2.wiper
  N8: Bela1.AOUT_GND, R11.Pin_0, R12.Pin_0
  N9: Bela1.AOUT_7, LED3.cathode
  N10: Bela1.AOUT_5, LED2.cathode
  N11: LED2.anode, R11.Pin_1
  N12: LED3.anode, R12.Pin_1

notes:
  Pins are numbered below the potentiometer
  Pin 1 to GND
  Pin 2 to Bela Analog Input
  Pin 3 to 3.3V<module fritzingVersion="0.9.4.2019-12-01.CD-498-0-a1ffcea">
  <boundingRects>
  <boundingRect rect="0 0 0 0" name="Schematic View"/>
  <boundingRect rect="0 0 0 0" name="PCB View"/>
  <boundingRect rect="49.338 88.6553 19.3203 68.6232" name="Breadboard View"/>
  </boundingRects>
  <instances>
  <instance moduleIdRef="5mmColorLEDModuleID" path="/Applications/Fritzing.app/Contents/MacOS/fritzing-parts/core/LED-generic-5mm.fzp" modelIndex="5961">
  <property name="color" value="Red (633nm)"/>
  <title>LED1</title>
  <views>
  <breadboardView layer="breadboard">
  <geometry z="2.50006" x="49.338" y="120.77">
  <transform m12="0" m21="0" m13="0" m32="36.5085" m11="-1" m23="0" m22="-1" m31="19.3203" m33="1"/>
  </geometry>
  <connectors>
  <connector connectorId="connector0" layer="breadboard">
  <geometry x="5.6583" y="36.5085"/>
  <leg>
  <point x="0" y="0"/>
  <bezier/>
  <point x="0" y="30.7701"/>
  <bezier/>
  </leg>
  <connects/>
  </connector>
  <connector connectorId="connector1" layer="breadboard">
  <geometry x="14.661" y="36.5085"/>
  <leg>
  <point x="0" y="0"/>
  <bezier/>
  <point x="0" y="30.7701"/>
  <bezier/>
  </leg>
  <connects/>
  </connector>
  </connectors>
  </breadboardView>
  <pcbView layer="copper0">
  <geometry z="5.50008" x="313.015" y="40.567"/>
  <titleGeometry visible="true" xOffset="21.969" yOffset="-7" textColor="#000000" fontSize="5" x="334.984" y="33.567" z="12.5">
  <displayKey key=""/>
  </titleGeometry>
  <connectors>
  <connector connectorId="connector0" layer="copper0">
  <geometry x="0" y="0"/>
  <connects/>
  </connector>
  <connector connectorId="connector1" layer="copper0">
  <geometry x="0" y="0"/>
  <connects/>
  </connector>
  </connectors>
  </pcbView>
  <schematicView layer="schematic">
  <geometry z="2.50006" x="230.624" y="458.729"/>
  <titleGeometry visible="true" xOffset="1.54897" yOffset="-24.2192" textColor="#000000" fontSize="5" x="232.173" y="434.51" z="6.50002">
  <displayKey key=""/>
  <displayKey key="part number"/>
  <displayKey key="color"/>
  <displayKey key="current"/>
  </titleGeometry>
  <connectors>
  <connector connectorId="connector0" layer="schematic">
  <geometry x="0" y="0"/>
  <connects/>
  </connector>
  <connector connectorId="connector1" layer="schematic">
  <geometry x="0" y="0"/>
  <connects/>
  </connector>
  </connectors>
  </schematicView>
  </views>
  </instance>
  </instances>
  </module>

custom parts:
  Bela: A Fritzing part for Bela
  SparkFun-LSM9DS1-Breakout: The LSM9DS1 is a versatile, motion-sensing system-in-a-chip. It houses a 3-axis accelerometer, 3-axis gyroscope, and 3-axis magnetometer – nine degrees of freedom (9DOF) in a single IC! The LSM9DS1 is equipped with a digital interface, but even that is flexible: it supports both I2C and SPI, so you’ll be hard-pressed to find a microcontroller it doesn’t work with. Each sensor in the LSM9DS1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
  SoftPot Membrane Potentiometer - 50mm: These are very thin variable potentiometers. By pressing down on various parts of the strip, the resistance linearly changes from 100Ohms to 10,000Ohms allowing the user to very accurately calculate the relative position on the strip. Can be used as an accurate positional indicator for CNC head positioning, variable user input (volume level input for example), straight user input (multiple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
