# Fritzing sketch robiohead_2022-09 (saved by Fritzing 0.9.4)
breadboards: 1

parts:
  Bela1 = Bela
  J1 = Basic Force Sensing Resistor (FSR) [package=THT]
  LED1 = LED - 5mm [color="Red (633nm)" package="5 mm [THT]"]
  S1 = Pushbutton [package="[THT]"]
  LED2 = LED - 5mm [color="Yellow (592nm)" package="5 mm [THT]"]
  LED3 = LED - 5mm [color="Blue (430nm)" package="5 mm [THT]"]
  LED4 = LED - 5mm [color="White (4500K)" package="5 mm [THT]"]
  R1 = Resistor [tolerance=±5% resistance=220 package=THT]
  R2 = Resistor [tolerance=±5% resistance=220 package=THT]
  R3 = Resistor [tolerance=±5% resistance=220 package=THT]
  R4 = Resistor [tolerance=±5% resistance=220 package=THT]
  R5 = Resistor [tolerance=±5% resistance=10k package=THT]
  R6 = Resistor [tolerance=±5% resistance=10k package=THT]
  R7 = Rotary Potentiometer (Small) [maximum_resistance=100kΩ package=THT]

nets:
  N1: Bela1.P9_01_GND, Bela1.P9_02_GND, R4.Pin_1, R5.Pin_1, R6.Pin_1, R7.leg2
  N2: Bela1.P9_03_3.3V, Bela1.P9_04_3.3V, J1.pin_1, S1.Pin_3, S1.Pin_4, R7.leg1
  N3: Bela1.P9_12_D6, LED1.anode
  N4: Bela1.P9_14_D7, S1.Pin_1, S1.Pin_2, R6.Pin_0
  N5: Bela1.AIN_1, J1.pin_0, R5.Pin_0
  N6: Bela1.AIN_0, R7.wiper
  N7: Bela1.AOUT_GND, R1.Pin_0, R2.Pin_0, R3.Pin_0
  N8: Bela1.AOUT_7, LED2.anode
  N9: Bela1.AOUT_6, LED3.anode
  N10: Bela1.AOUT_5, LED4.anode
  N11: LED1.cathode, R4.Pin_0
  N12: LED2.cathode, R1.Pin_1
  N13: LED3.cathode, R2.Pin_1
  N14: LED4.cathode, R3.Pin_1

custom parts:
  Bela: A Fritzing part for Bela
