# Fritzing sketch workshp_2022-10-14_resolution (saved by Fritzing 0.9.4)
breadboards: 1

parts:
  Bela1 = Bela
  R1 = Resistor [tolerance=±5% resistance=1k package="2010 [SMD]"]
  S8 = Momentary Switch [package=ksa_sealed_tac_switch]
  R2 = Rotary Potentiometer (Small) [maximum_resistance=100kΩ package=THT]

nets:
  N1: Bela1.P9_01_GND, R1.Pin_0, R2.leg2
  N2: Bela1.P9_03_3.3V, S8.1, R2.leg1
  N3: Bela1.AIN_0, R2.wiper
  N4: R1.Pin_1, S8.3

custom parts:
  Bela: A Fritzing part for Bela
